# Fritzing sketch openhaardvuur (saved by Fritzing 1.0.1rc)

parts:
  Mod1 = Raspberry Pi Pico
  OLED_I2C1 = OLED 128x64 I2C Monochrome Display

nets:
  N1: Mod1.pin_6, OLED_I2C1.SDA
  N2: Mod1.pin_7, OLED_I2C1.SCK
  N3: Mod1.pin_36, OLED_I2C1.VDD
  N4: Mod1.pin_38, Mod1.pin_42, OLED_I2C1.GND

custom parts:
  Raspberry Pi Pico: Raspberry Pi Pico. Based around the RP2040 microcontroller the Pico is a low cost microcontroller device bringing Raspberry Pi quality, cost, and easy of use to the microcontroller space. Jan 2021, Split part in to two versions: tht (this one) and SMD. This one will drill holes for a .1 in header in pcb to allow plugging in the module as well as providing pads to solder the module to the top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
